# Fritzing sketch board (saved by Fritzing 0.9.6b)
circuit board: 4.27447cm x 5.82338cm

parts:
  1KΩ = Resistor [tolerance=±5% power=0.25 resistance=1k package=THT]
  4_7KΩ = Resistor [tolerance=±5% power=0.25 resistance=4.7k package=THT]
  1000µF = Electrolytic Capacitor [capacitance=1µF voltage=16V package="200 mil [THT, electrolytic]"]
  DHT22 = screw terminal, 3 pins
  PHRE = Screw terminal - 2 pins [package=THT]
  WeMos_D1_Mini1 = WeMos D1 Mini
  LED_Matrix = screw terminal, 3 pins
  Power = Screw terminal - 2 pins [package=THT]
  MP3 = Screw terminal - 2 pins [package=THT]

nets:
  N1: 1KΩ.Pin_0, 1000µF.-, DHT22.pin1, WeMos_D1_Mini1.G, LED_Matrix.pin1, Power.pin1
  N2: 1KΩ.Pin_1, PHRE.pin1, WeMos_D1_Mini1.A0
  N3: 4_7KΩ.Pin_0, DHT22.pin3, PHRE.pin2, WeMos_D1_Mini1.3V3
  N4: 4_7KΩ.Pin_1, DHT22.pin2, WeMos_D1_Mini1.D1
  N5: 1000µF.+, WeMos_D1_Mini1.5V, LED_Matrix.pin3, Power.pin2
  N6: WeMos_D1_Mini1.D2, LED_Matrix.pin2
  N7: WeMos_D1_Mini1.D7, MP3.pin2
  N8: WeMos_D1_Mini1.D8, MP3.pin1

notes:
  (c) Daniel Pfister 2021
  GND
  5V
  SIG
  3,3V
